# Fritzing sketch SimplestSketch (saved by Fritzing 0.4.3b)

parts:
  Minia1 = Minia
  R1 = Rotary Potentiometer (Small)

nets:
  N1: Minia1.connector7, R1.leg1
  N2: Minia1.connector8, R1.leg2
  N3: Minia1.connector9, R1.wiper
